// Digital circuit 4 bit subtractor (1) (1).dig as structural Verilog
module _4_bit_subtractor__1___1 (
  input  [3:0] A,
  input  [3:0] B,
  output [3:0] Sum
);

  wire adder_1_p5, adder_2_p5, adder_3_p5, xor_1_out, xor_2_out, xor_3_out, xor_4_out;

  xor xor_1 (xor_1_out, B[0], 1'b1);
  xor xor_2 (xor_2_out, B[1], 1'b1);
  xor xor_3 (xor_3_out, B[2], 1'b1);
  xor xor_4 (xor_4_out, B[3], 1'b1);
  // Adder adder_1: pin names not known; wires that end beside it: A[0], xor_1_out, 1'b1, Sum[0], adder_1_p5
  // Adder adder_2: pin names not known; wires that end beside it: A[1], xor_2_out, adder_1_p5, Sum[1], adder_2_p5
  // Adder adder_3: pin names not known; wires that end beside it: A[2], xor_3_out, adder_2_p5, Sum[2], adder_3_p5
  // Adder adder_4: pin names not known; wires that end beside it: A[3], xor_4_out, adder_3_p5, Sum[3]
endmodule
