// Digital circuit 4bi_ALU.dlogic.dig as structural Verilog
module _4bi_ALU_dlogic (
  input  [3:0] A,
  input  [3:0] B,
  input  [2:0] Control_Signal,
  output Overflow,
  output Zero_Flag,
  output SLT_Logic,
  output [3:0] Choosen_Operation
);

  wire [3:0] _4_bit_adder_1_sum, _4_bit_subtractor_1_p3, _4bit_and_1_p3, _4bit_or_1_p3, _4bit_xor_1_p3;

  // _4bit_XOR _4bit_xor_1: pin names not known; wires that end beside it: A, B, _4bit_xor_1_p3
  // _4bit_OR _4bit_or_1: pin names not known; wires that end beside it: A, B, _4bit_or_1_p3
  // _4bit_AND _4bit_and_1: pin names not known; wires that end beside it: A, B, _4bit_and_1_p3
  _4_bit_adder _4_bit_adder_1 (.A(A), .B(B), .Sum(_4_bit_adder_1_sum), .C_out(Overflow));
  // _4_bit_subtractor _4_bit_subtractor_1: pin names not known; wires that end beside it: A, B, _4_bit_subtractor_1_p3
  // SLT slt_1: pin names not known; wires that end beside it: A, B, SLT_Logic
  Multiplexer #(.Bits(4), .Selector_Bits(3)) multiplexer_1 (
    .sel(Control_Signal), .in_0(_4_bit_adder_1_sum), .in_1(_4_bit_subtractor_1_p3), .in_2(_4bit_and_1_p3),
    .in_3(_4bit_or_1_p3), .in_4(_4bit_xor_1_p3), .in_5(4'b0000), .in_6(4'b0000), .in_7(4'b0000),
    .out(Choosen_Operation));
  // _4_bit_zero_flag _4_bit_zero_flag_1: pin names not known; wires that end beside it: _4_bit_adder_1_sum, Zero_Flag

  // Notes on the sheet:
  //   Overflow: Carry out from the Adder function
endmodule
